// Logisim project flipflooop.circ as structural Verilog: 4 circuits, main circuit main
module main (
);

  wire clock_1_out, CONTROLLER_out_5, CONTROLLER_out_6, CONTROLLER_out_7, CONTROLLER_out_8, CONTROLLER_out_9,
       COUNTER_out_2, COUNTER_out_3, COUNTER_out_4, COUNTER_out_5;

  Controller CONTROLLER (
    .out_5(CONTROLLER_out_5), .out_6(CONTROLLER_out_6), .out_7(CONTROLLER_out_7), .out_8(CONTROLLER_out_8),
    .out_9(CONTROLLER_out_9), .in_1(COUNTER_out_2), .in_2(COUNTER_out_3), .in_3(COUNTER_out_4),
    .in_4(COUNTER_out_5));
  Counter COUNTER (
    .in_1(clock_1_out), .out_2(COUNTER_out_2), .out_3(COUNTER_out_3), .out_4(COUNTER_out_4),
    .out_5(COUNTER_out_5));
  Clock clock_1 (.out(clock_1_out));
  LED led_1 (.in(CONTROLLER_out_5));
  LED led_2 (.in(CONTROLLER_out_5));
  LED led_3 (.in(CONTROLLER_out_6));
  LED led_4 (.in(CONTROLLER_out_6));
  LED led_5 (.in(CONTROLLER_out_7));
  LED led_6 (.in(CONTROLLER_out_7));
  LED led_7 (.in(CONTROLLER_out_8));
  LED led_8 (.in(CONTROLLER_out_8));
  LED led_9 (.in(CONTROLLER_out_5));
  LED led_10 (.in(CONTROLLER_out_5));
  LED led_11 (.in(CONTROLLER_out_6));
  LED led_12 (.in(CONTROLLER_out_5));
  LED led_13 (.in(CONTROLLER_out_6));
  LED led_14 (.in(CONTROLLER_out_7));
  LED led_15 (.in(CONTROLLER_out_6));
  LED led_16 (.in(CONTROLLER_out_7));
  LED led_17 (.in(CONTROLLER_out_8));
  LED led_18 (.in(CONTROLLER_out_7));
  LED led_19 (.in(CONTROLLER_out_8));
  LED led_20 (.in(CONTROLLER_out_8));
  LED led_21 (.in(CONTROLLER_out_9));
  LED led_22 (.in(CONTROLLER_out_9));
  LED led_23 (.in(CONTROLLER_out_9));
  LED led_24 (.in(CONTROLLER_out_9));
  LED led_25 (.in(CONTROLLER_out_9));
  LED led_26 (.in(CONTROLLER_out_9));
  LED led_27 (.in(CONTROLLER_out_9));
  LED led_28 (.in(CONTROLLER_out_9));
  LED led_29 (.in(CONTROLLER_out_9));
  LED led_30 (.in(CONTROLLER_out_9));
  LED led_31 (.in(CONTROLLER_out_9));
  LED led_32 (.in(CONTROLLER_out_9));
  LED led_33 (.in(CONTROLLER_out_5));
  LED led_34 (.in(CONTROLLER_out_5));
  LED led_35 (.in(CONTROLLER_out_6));
  LED led_36 (.in(CONTROLLER_out_5));
  LED led_37 (.in(CONTROLLER_out_6));
  LED STATE_5 (.in(CONTROLLER_out_5));
  LED led_38 (.in(CONTROLLER_out_7));
  LED led_39 (.in(CONTROLLER_out_6));
  LED led_40 (.in(CONTROLLER_out_7));
  LED STATE_4 (.in(CONTROLLER_out_6));
  LED led_41 (.in(CONTROLLER_out_8));
  LED led_42 (.in(CONTROLLER_out_7));
  LED led_43 (.in(CONTROLLER_out_8));
  LED STATE_3 (.in(CONTROLLER_out_7));
  LED led_44 (.in(CONTROLLER_out_9));
  LED led_45 (.in(CONTROLLER_out_8));
  LED led_46 (.in(CONTROLLER_out_9));
  LED led_47 (.in(CONTROLLER_out_9));
  LED STATE_2 (.in(CONTROLLER_out_8));
  LED led_48 (.in(CONTROLLER_out_9));
  LED led_49 (.in(CONTROLLER_out_9));
  LED led_50 (.in(CONTROLLER_out_9));
  LED led_51 (.in(CONTROLLER_out_9));
  LED led_52 (.in(CONTROLLER_out_9));
  LED led_53 (.in(CONTROLLER_out_9));
  LED led_54 (.in(CONTROLLER_out_9));
  LED STATE_1 (.in(CONTROLLER_out_9));
endmodule

module Counter (
  input  in_1,
  output out_2,
  output out_3,
  output out_4,
  output out_5
);

  wire d_ff_1_qn, d_ff_2_qn, d_ff_3_qn, d_ff_4_qn, RESET_out_4;

  CounterReset RESET (.out_4(RESET_out_4), .in_1(out_3), .in_2(out_5), .in_3(out_4));
  D_Flip_Flop d_ff_1 (.clk(in_1), .D(d_ff_1_qn), .Q(out_2), .Qn(d_ff_1_qn), .reset(RESET_out_4));  // open: preset, en
  D_Flip_Flop d_ff_2 (
    .clk(d_ff_1_qn), .D(d_ff_2_qn), .Q(out_3), .Qn(d_ff_2_qn), .reset(RESET_out_4));  // open: preset, en
  D_Flip_Flop d_ff_3 (
    .clk(d_ff_2_qn), .D(d_ff_3_qn), .Q(out_4), .Qn(d_ff_3_qn), .reset(RESET_out_4));  // open: preset, en
  D_Flip_Flop d_ff_4 (
    .clk(d_ff_3_qn), .D(d_ff_4_qn), .Q(out_5), .Qn(d_ff_4_qn), .reset(RESET_out_4));  // open: preset, en
endmodule

module Controller (
  input  in_1,
  input  in_2,
  input  in_3,
  input  in_4,
  output out_5,
  output out_6,
  output out_7,
  output out_8,
  output out_9
);

  wire _1_out, _3_out, _4_out, _5_out, _6_out, _7_out, _8_out, _9_out, _10_out, _11_out, _13_out, not_1_out,
       not_2_out, not_3_out, not_4_out;

  or STATE_5 (out_5, _13_out, _11_out, _10_out, _9_out);
  and _3 (_3_out, in_1, in_2, not_4_out, not_3_out);
  and _1 (_1_out, in_1, not_2_out, not_4_out, not_3_out);
  or STATE_4 (out_6, _11_out, _13_out, _8_out, _7_out);
  and _4 (_4_out, not_1_out, not_2_out, in_3, not_3_out);
  or STATE_3 (out_7, _11_out, _5_out, _13_out, _6_out);
  and _6 (_6_out, not_1_out, in_2, not_3_out, in_3);
  and _5 (_5_out, in_1, not_2_out, in_3, not_3_out);
  not not_1 (not_1_out, in_1);
  or STATE_2 (out_8, _13_out, _11_out, _4_out, _3_out);
  and _7 (_7_out, in_1, in_2, in_3, not_3_out);
  not not_2 (not_2_out, in_2);
  not not_3 (not_3_out, in_4);
  not not_4 (not_4_out, in_3);
  or STATE_1 (out_9, _1_out, _3_out, _4_out, _5_out, _6_out, _13_out, _7_out, _8_out, _9_out, _10_out, _11_out);
  and _9 (_9_out, in_1, not_2_out, not_4_out, in_4);
  and _8 (_8_out, not_1_out, not_2_out, not_4_out, in_4);
  and _10 (_10_out, not_1_out, in_2, not_4_out, in_4);
  and _11 (_11_out, in_1, in_2, not_4_out, in_4);
  and _13 (_13_out, in_1, not_2_out, in_3, in_4);

  // Notes on the sheet:
  //   4-BIT DECODER
endmodule

module CounterReset (
  input  in_1,
  input  in_2,
  input  in_3,
  output out_4
);

  wire and_2_out;

  and and_1 (out_4, and_2_out, in_3);
  and and_2 (and_2_out, in_1, in_2);
endmodule
